// Logisim project control-logic.circ as structural Verilog: 1 circuit, main circuit control_logic
module control_logic (
  input  [31:0] Instruction,
  input  BrEq,
  input  BrLt,
  output PCSel,
  output RegWEn,
  output [2:0] ImmSel,
  output BrUn,
  output ASel,
  output BSel,
  output [3:0] ALUSel,
  output MemWEn,
  output [1:0] WBSel
);

  wire and_1_out, and_2_out, and_3_out, and_4_out, and_5_out, and_6_out, and_7_out, and_8_out, and_10_out,
       and_11_out, comparator_1_eq, comparator_2_eq, comparator_3_eq, comparator_4_eq, comparator_5_eq,
       comparator_6_eq, comparator_9_eq, comparator_10_eq, comparator_11_eq, comparator_12_eq,
       comparator_13_eq, comparator_14_eq, comparator_15_eq, comparator_16_eq, comparator_17_eq,
       comparator_18_eq, not_1_out, not_2_out, not_3_out, not_4_out, or_1_out, or_2_out, or_4_out;
  wire [2:0] adder_1_out, adder_3_out, adder_4_out, adder_5_out, multiplexer_1_out, multiplexer_4_out,
       multiplexer_6_out, multiplexer_7_out, multiplexer_10_out;
  wire [3:0] adder_2_out, ALUSelI, ALUSelR, bit_extender_1_out, bit_extender_2_out, multiplexer_2_out,
       multiplexer_8_out;
  wire [15:0] rom_1_data;

  assign bit_extender_1_out = {{1{Instruction[14]}}, Instruction[14:12]};  // Bit_Extender bit_extender_1
  Comparator #(.width(3)) comparator_1 (.a(Instruction[14:12]), .b(3'b000), .eq(comparator_1_eq));  // open: gt, lt
  Comparator #(.width(3)) comparator_2 (.a(Instruction[14:12]), .b(3'b001), .eq(comparator_2_eq));  // open: gt, lt
  Comparator #(.width(3)) comparator_3 (.a(Instruction[14:12]), .b(3'b100), .eq(comparator_3_eq));  // open: gt, lt
  Comparator #(.width(3)) comparator_4 (.a(Instruction[14:12]), .b(3'b101), .eq(comparator_4_eq));  // open: gt, lt
  Comparator #(.width(3)) comparator_5 (.a(Instruction[14:12]), .b(3'b110), .eq(comparator_5_eq));  // open: gt, lt
  Comparator #(.width(3)) comparator_6 (.a(Instruction[14:12]), .b(3'b111), .eq(comparator_6_eq));  // open: gt, lt
  Comparator #(.width(3)) comparator_7 (.a(Instruction[6:4]), .b(3'b010), .eq(MemWEn));  // open: gt, lt
  Adder #(.width(3)) adder_1 (.a(3'b000), .b(3'b001), .out(adder_1_out));  // open: cin, cout
  ROM #(.addrWidth(6), .dataWidth(16)) rom_1 (.data(rom_1_data));  // open: addr
  Comparator #(.width(7)) comparator_8 (.a(7'b0110011), .b(Instruction[6:0]), .eq(BSel));  // open: gt, lt
  Adder #(.width(4)) adder_2 (.a(bit_extender_1_out), .b(4'b1000), .out(adder_2_out));  // open: cin, cout
  not not_1 (not_1_out, Instruction[12]);
  Comparator #(.width(3)) comparator_9 (.a(Instruction[14:12]), .b(3'b101), .eq(comparator_9_eq));  // open: gt, lt
  Comparator #(.width(2)) comparator_10 (.a(Instruction[5:4]), .b(2'b10), .eq(comparator_10_eq));  // open: gt, lt
  and and_1 (and_1_out, Instruction[30], not_1_out);
  or or_1 (or_1_out, comparator_6_eq, comparator_5_eq);
  Multiplexer #(.width(3)) multiplexer_1 (
    .in0(3'b000), .in1(adder_1_out), .out(multiplexer_1_out), .sel(Instruction[6]));
  assign bit_extender_2_out = {{1{1'b0}}, Instruction[14:12]};  // Bit_Extender bit_extender_2
  not not_2 (not_2_out, comparator_10_eq);
  Multiplexer #(.width(4)) multiplexer_2 (
    .in0(bit_extender_1_out), .in1(adder_2_out), .out(multiplexer_2_out), .sel(or_2_out));
  or or_2 (or_2_out, Instruction[30], Instruction[25]);
  Comparator #(.width(7)) comparator_11 (.a(Instruction[6:0]), .b(7'b1100011), .eq(comparator_11_eq));  // open: gt, lt
  Comparator #(.width(7)) comparator_12 (.a(Instruction[6:0]), .b(7'b1101111), .eq(comparator_12_eq));  // open: gt, lt
  Comparator #(.width(7)) comparator_13 (.a(Instruction[6:0]), .b(7'b0010111), .eq(comparator_13_eq));  // open: gt, lt
  not not_3 (not_3_out, BrEq);
  not not_4 (not_4_out, BrLt);
  Adder #(.width(3)) adder_3 (.a(multiplexer_1_out), .b(3'b001), .out(adder_3_out));  // open: cin, cout
  Multiplexer #(.width(4)) multiplexer_3 (.in0(bit_extender_2_out), .in1(4'b1101), .out(ALUSelI), .sel(and_2_out));
  and and_2 (and_2_out, Instruction[30], comparator_9_eq);
  and and_3 (and_3_out, BrEq, comparator_1_eq);
  and and_4 (and_4_out, not_3_out, comparator_2_eq);
  and and_5 (and_5_out, BrLt, comparator_3_eq);
  and and_6 (and_6_out, comparator_4_eq, not_4_out);
  and and_7 (and_7_out, comparator_5_eq, BrLt);
  and and_8 (and_8_out, not_4_out, comparator_6_eq);
  Multiplexer #(.width(3)) multiplexer_4 (
    .in0(multiplexer_1_out), .in1(adder_3_out), .out(multiplexer_4_out), .sel(Instruction[5]));
  or or_3 (RegWEn, Instruction[2], not_2_out);
  Multiplexer #(.width(4)) multiplexer_5 (.in0(multiplexer_2_out), .in1(4'b1100), .out(ALUSelR), .sel(and_1_out));
  Adder #(.width(3)) adder_4 (.a(multiplexer_4_out), .b(3'b001), .out(adder_4_out));  // open: cin, cout
  nor nor_1 (ASel, comparator_11_eq, comparator_12_eq, comparator_13_eq);
  Multiplexer #(.width(3)) multiplexer_6 (
    .in0(multiplexer_4_out), .in1(adder_4_out), .out(multiplexer_6_out), .sel(Instruction[3]));
  or or_4 (or_4_out, and_5_out, and_3_out, and_4_out, and_6_out, and_7_out, and_8_out);
  Adder #(.width(3)) adder_5 (.a(multiplexer_6_out), .b(3'b001), .out(adder_5_out));  // open: cin, cout
  and and_9 (BrUn, comparator_11_eq, or_1_out);
  Multiplexer #(.width(3)) multiplexer_7 (
    .in0(multiplexer_6_out), .in1(adder_5_out), .out(multiplexer_7_out), .sel(Instruction[2]));
  Multiplexer #(.select(2), .width(4)) multiplexer_8 (
    .in0(4'b0000), .in1(ALUSelI), .in2(4'b0000), .in3(ALUSelR), .out(multiplexer_8_out),
    .sel(Instruction[5:4]));
  Comparator #(.width(7)) comparator_14 (.a(Instruction[6:0]), .b(7'b0110111), .eq(comparator_14_eq));  // open: gt, lt
  and and_10 (and_10_out, comparator_11_eq, or_4_out);
  Multiplexer #(.width(4)) multiplexer_9 (.in0(multiplexer_8_out), .in1(4'b1111), .out(ALUSel), .sel(comparator_14_eq));
  Comparator #(.width(7)) comparator_15 (.a(Instruction[6:0]), .b(7'b1101111), .eq(comparator_15_eq));  // open: gt, lt
  Comparator #(.width(7)) comparator_16 (.a(Instruction[6:0]), .b(7'b1100111), .eq(comparator_16_eq));  // open: gt, lt
  Multiplexer #(.width(3)) multiplexer_10 (
    .in0(multiplexer_7_out), .in1(3'b011), .out(multiplexer_10_out), .sel(comparator_17_eq));
  Comparator #(.width(4)) comparator_17 (.a(4'b0111), .b(Instruction[3:0]), .eq(comparator_17_eq));  // open: gt, lt
  or or_5 (PCSel, comparator_15_eq, and_10_out, comparator_16_eq);
  Comparator #(.width(3)) comparator_18 (.a(3'b110), .b(Instruction[6:4]), .eq(comparator_18_eq));  // open: gt, lt
  and and_11 (and_11_out, comparator_17_eq, comparator_18_eq);
  Multiplexer #(.width(3)) multiplexer_11 (.in0(multiplexer_10_out), .in1(3'b000), .out(ImmSel), .sel(and_11_out));

  assign WBSel = {Instruction[6], Instruction[4]};

  // Other names for the same wires on the sheet: opcode[6:0] = Instruction[6:0]; funct3[2:0] = Instruction[14:12];
  //   funct7[6:0] = Instruction[31:25]

  // Notes on the sheet:
  //   INPUTS to your circuit
  //   Connect ROM Input here ->
  //   ROM FOR CONTROL LOGIC
  //   DON'T CHANGE THE LOCATIONS OF THE INPUTS AND OUTPUTS!
  //   This is only if you choose to do the ROM option
  //   CONNECT
  //   WIRE
  //   TO
  //   USE
  //   ROM
  //   OUTPUT from your circuit
  //   Reminder: If using ROM, use combinational logic for PCSel
endmodule
